# Fritzing sketch rtu_QoSFreeRTOS (saved by Fritzing 0.9.3b)
breadboards: 3

parts:
  Component1 = RS485_XY-017 [part_number=XY-017]
  Component2 = RS485_XY-017 [part_number=XY-017]
  Component3 = RS485_XY-017 [part_number=XY-017]
  WeMos_D1_R1 = WeMos D1 R2
  WeMos_D1_R2 = WeMos D1 R2
  WeMos_D1_R3 = WeMos D1 R2
  LED1 = LED - 3mm [color="Blue (430nm)" package="3 mm [THT]"]
  LED2 = LED - 3mm [color="Blue (430nm)" package="3 mm [THT]"]
  LED3 = LED - 3mm [color="Blue (430nm)" package="3 mm [THT]"]
  LED4 = LED - 3mm [color="Red (633nm)" package="3 mm [THT]"]
  S1 = Pushbutton [package=THT]
  S2 = Pushbutton [package=THT]
  S3 = Pushbutton [package=THT]
  S4 = Pushbutton [package=THT]
  R1 = Resistor [tolerance=±5% resistance=120 package=THT]

nets:
  N1: Component1.GND#0, WeMos_D1_R3.GND#20
  N2: Component1.A, Component2.A, Component3.A, R1.Pin_0
  N3: Component1.B, Component2.B, Component3.B, R1.Pin_1
  VCC: Component1.VCC, WeMos_D1_R3.3.3V
  N4: Component1.TXD, WeMos_D1_R3.D0/RX
  N5: Component1.GND#5, Component2.GND#5, Component3.GND#5
  N6: Component1.RXD, WeMos_D1_R3.D1/TX
  N7: Component2.GND#0, WeMos_D1_R1.GND#20
  VCC_2: Component2.VCC, WeMos_D1_R1.3.3V
  N8: Component2.TXD, WeMos_D1_R1.D0/RX
  N9: Component2.RXD, WeMos_D1_R1.D1/TX
  N10: Component3.GND#0, WeMos_D1_R2.GND#15
  VCC_3: Component3.VCC, WeMos_D1_R2.3.3V
  N11: Component3.TXD, WeMos_D1_R2.D0/RX, WeMos_D1_R3.5V
  N12: Component3.RXD, WeMos_D1_R2.D1/TX
  N13: WeMos_D1_R1.D2, S1.leg1
  N14: WeMos_D1_R1.D3, S2.leg1
  N15: WeMos_D1_R1.D12, LED4.anode
  N16: WeMos_D1_R1.D13, LED3.anode
  N17: WeMos_D1_R1.GND#21, LED3.cathode, LED4.cathode, S1.leg0, S2.leg0
  N18: WeMos_D1_R2.D2, S4.leg1
  N19: WeMos_D1_R2.D13, LED2.anode
  N20: WeMos_D1_R2.GND#20, LED2.cathode, S4.leg0
  N21: WeMos_D1_R3.D2, S3.leg0
  N22: WeMos_D1_R3.D13, LED1.anode
  N23: WeMos_D1_R3.GND#15, LED1.cathode, S3.leg1

notes:
  Master
  Slave 1
  Slave 2

custom parts:
  RS485_XY-017: Commercially available RS485 to RS232 TTL Module
  WeMos D1 R2: The D1 R2 is a mini wifi board based on the ESP-8266EX.
